# Fritzing sketch diagrama-esquematico-pendulo-helice (saved by Fritzing 0.9.2b)

parts:
  Componente1 = Arduino Uno (Rev3) - ICSP
  R1 = Rotary Potentiometer (Small) [maximum_resistance=10kΩ package=THT]
  R2 = Rotary Potentiometer (Small) [maximum_resistance=10kΩ package=THT]
  R3 = Resistor [tolerance=±5% resistance=10k package="2010 [SMD]"]
  R4 = Resistor [tolerance=±5% resistance=4.7k package="2010 [SMD]"]
  Q1 = Basic FET N-Channel [package="TO220 [THT]"]
  M1 = DC Motor
  Componente2 = Breadboard Power Supply Board SMD

nets:
  N1: Componente1.A1, R1.wiper
  N2: Componente1.A2, R2.wiper
  GND: Componente1.GND, R1.leg1, R2.leg2, R3.Pin_1, Q1.source, Componente2.GND
  N3: Componente1.D9_PWM, R4.Pin_0
  5V: Componente1.5V, R1.leg2, R2.leg1, Componente2.VIN
  N4: R3.Pin_0, R4.Pin_1
  N5: Q1.drain, M1.pin_2
  N6: M1.pin_1, Componente2.VCC

notes:
  potenciometro 10k ohm
  realimentação de posição
  motor de quadcóptero
  3.3V
  5V
  GND
  4k7 ohm
  10k ohm
  IRF3415
  Regulador de tensão
  de 5V para 3,3V
  referência de posição
  usuário
  A1
  A2
  Fonte 9V 2A
